# Fritzing sketch Pi_GPS_Box (saved by Fritzing 0.9.3b)

parts:
  Raspberry_Pi_Zero1 = Raspberry Pi Zero
  Part1 = OLED Monochrome 128x64 1.3 inch [part_number=938]
  Part2 = PowerBoost 1000 Basic
  U1 = SWITCH_SPDT [package=kps-1290]
  Part3 = Lithium Ion Polymer Battery 3.7v 2500mAh [part_number=328]
  Part4 = Adafruit Ultimate GPS v3 [part_number="Adafruit #746"]
  IC1 = 24LC16 [package=THT]
  R1 = Resistor [tolerance=±5% resistance=220 package="2512 [SMD]"]  # not connected

nets:
  3V3: Raspberry_Pi_Zero1.3v3, Raspberry_Pi_Zero1.3V3, Part1.VIN, Part4.VIN
  N1: Raspberry_Pi_Zero1.GPIO10, Part1.MOSI_SDA
  N2: Raspberry_Pi_Zero1.GPIO11, Part1.SCLK_SCK
  N3: Raspberry_Pi_Zero1.ID_SD, IC1.SDA_-_I2C_Data
  N4: Raspberry_Pi_Zero1.GPIO21, Part1.GND
  N5: Raspberry_Pi_Zero1.ID_SC, IC1.SCL_-_I2C_Clock
  N6: Raspberry_Pi_Zero1.GPIO8, Part1.CS
  N7: Raspberry_Pi_Zero1.GPIO24, Part1.RESET
  N8: Raspberry_Pi_Zero1.GPIO23, Part1.DC_SA0
  N9: Raspberry_Pi_Zero1.GPIO15, Part4.TX
  N10: Raspberry_Pi_Zero1.GPIO14, Part4.RX
  GND: Raspberry_Pi_Zero1.GND, Part2.GND, U1.O
  N11: Raspberry_Pi_Zero1.5V, Part2.5.0V
  N12: Part2.ENABLE, U1.P
  N13: Part2.VBAT, Part3.positive

custom parts:
  OLED Monochrome 128x64 1.3 inch: These displays are small, only about 1.3" diagonal, but very readable due to the high contrast of an OLED display. This display is made of 128x64 individual white OLED pixels, each one is turned on or off by the controller chip. Because the display makes its own light, no backlight is required. This reduces the power required to run the OLED and is why the display has such high contrast; we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
  PowerBoost 1000 Basic: The PowerBoost 1000 is a little DC/DC boost converter module that can run from 1.8V batteries or higher, and convert the battery output to 5.2V DC for running your 5V projects. At its heart is a TPS61030 boost converter from TI. This boost converter chip has some really nice extras such as low battery detection, 4A internal switch, synchronous conversion, excellent efficiency, and 700KHz high-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
  Lithium Ion Polymer Battery 3.7v 2500mAh: Lithium ion polymer (also known as 'lipo' or 'lipoly') batteries are thin, light and powerful. The output ranges from 4.2V when completely charged to 3.7V. This battery has a capacity of 2500mAh for a total of about 10 Wh. The batteries come pre-attached with a genuine 2-pin JST-PH connector as shown and include the necessary protection circuitry.
  Adafruit Ultimate GPS v3: We carry a few different GPS modules here in the Adafruit shop, but none that satisfied our every desire - that's why we designed this little GPS breakout board. We believe this is the Ultimate GPS module, so we named it that. It's got everything you want and more: -165 dBm sensitivity, 10 Hz updates, 66 channels 5V friendly design and only 20mA current draw Breadboard friendly + two mounting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
